# Fritzing sketch filtre (saved by Fritzing 0.9.3b)
breadboards: 2

parts:
  U1 = ESP 32 DEVKIT DOIT

nets:
  N1: U1.D22, U1.D18, U1.D5, U1.TX2, U1.RX2, U1.D4, U1.D2, U1.D15, U1.D0, U1.SD1

notes:
  Sortie Analogique
  Gnd
  Entrée Analogique
  Clk echantillonnage
